# Fritzing sketch Co2 Monitor (saved by Fritzing 0.9.3b)
circuit board: 8.49cm x 6.1cm
breadboards: 1

parts:
  M1 = RioRand LM2596
  TP1 = TP4056 [chip_label=TP4056 package="DIP (Dual Inline) [THT]"]
  GY1 = MPU-6050 Board GY-521 [form="♀ (female)" package=THT]
  JP1 = Header 2 [package=screwterminal-3.5mm-2_lock]
  R1 = Resistor [tolerance=±5% resistance=220 package=THT]
  JP3 = Header 4 [package=molex-1x4_lock]
  U1 = NodeMCU V1.0
  Switch = Square Pushbutton
  JP4 = Header 2 [package=screwterminal-3.5mm-2_lock]

nets (from the pcb view):
  N1: M1.Pin_1, TP1.pin3
  N2: M1.Pin_2, JP4.2
  N3: M1.Pin_3, GY1.pin1, JP3.3, U1.Vin
  N4: M1.Pin_4, GY1.pin2, R1.Pin_0, JP3.4, U1.GND
  N5: TP1.pin4, JP1.1
  N6: TP1.pin5, JP1.2
  N7: TP1.pin6, JP4.1
  N8: GY1.pin5, U1.D3
  N9: R1.Pin_1, U1.D5, Switch.leg1
  N10: JP3.1, U1.D1
  N11: JP3.2, U1.D2
  N12: U1.3V3, Switch.leg0

notes:
  CYBR node
  CO2 Monitor v1.1

custom parts:
  TP4056: A DIP stand-in part for whatever IC you want. With 6 pins on a 300mil dual inline package (DIP) footprint.
  MPU-6050 Board GY-521: Acelerometro y Giroscopio MPU-6050 Board GY-521
  NodeMCU V1.0: ESP8266 based NodeMCU
